# Fritzing sketch lab02 (saved by Fritzing 0.8.0b)
breadboards: 1

parts:
  AND = SN74LS32N [package="DIP14 [THT]"]
  R1 = Resistor [tolerance=±5% resistance=220 package="0805 [SMD]"]
  LED1 = LED - 3mm [color="Red (633nm)" package="3 mm [THT]"]
  AND_2 = SN74LS32N [package="DIP14 [THT]"]
  NOT = SN74LS14N [package="DIP14 [THT]"]
  A0 = Round Pushbutton
  A1 = Round Pushbutton
  B0 = Round Pushbutton
  B1 = Round Pushbutton
  XOR = SN74LS32N [package="DIP14 [THT]"]
  R2 = Resistor [tolerance=±5% resistance=220 package="0805 [SMD]"]
  LED2 = LED - 3mm [color="Red (633nm)" package="3 mm [THT]"]
  R3 = Resistor [tolerance=±5% resistance=220 package="0805 [SMD]"]
  LED3 = LED - 3mm [color="Red (633nm)" package="3 mm [THT]"]
  R4 = Resistor [tolerance=±5% resistance=220 package="0805 [SMD]"]
  LED4 = LED - 3mm [color="Red (633nm)" package="3 mm [THT]"]

nets:
  N1: AND.1A, AND.2A, A0.leg1
  N2: AND.1B, AND.4A, B0.leg1
  N3: AND.1Y, R1.Pin_0, NOT.1A
  N4: AND.2B, AND_2.2B, B1.leg1
  N5: AND.2Y, AND.3B, XOR.1A
  GND: AND.GND, LED1.cathode, AND_2.GND, NOT.GND, XOR.GND, LED2.cathode, LED3.cathode, LED4.cathode
  N6: AND.3Y, R3.Pin_0
  N7: AND.3A, AND.4Y, XOR.1B
  N8: AND.4B, AND_2.2A, A1.leg1
  5V: AND.Vcc, AND_2.Vcc, NOT.VCC, A0.leg0, A1.leg0, B0.leg0, B1.leg0, XOR.Vcc
  N9: R1.Pin_1, LED1.anode
  N10: AND_2.1A, NOT.1Y
  N11: AND_2.1B, AND_2.2Y
  N12: AND_2.1Y, R4.Pin_1
  N13: XOR.1Y, R2.Pin_0
  N14: R2.Pin_1, LED2.anode
  N15: R3.Pin_1, LED3.anode
  N16: R4.Pin_0, LED4.anode
