// Logisim project lab032schem.circ as structural Verilog: 1 circuit, main circuit main
module main (
);

  wire and_1_out, and_2_out, and_3_out, and_4_out, not_1_out, not_2_out, or_1_out, undriven, undriven_2,
       undriven_3, undriven_4, undriven_5, undriven_6;

  not not_1 (not_1_out, undriven_5);
  not not_2 (not_2_out, undriven_6);
  and and_1 (and_1_out, not_2_out, not_1_out, undriven);
  and and_2 (and_2_out, undriven_6, not_1_out, undriven_2);
  and and_3 (and_3_out, not_2_out, undriven_5, undriven_3);
  and and_4 (and_4_out, undriven_6, undriven_5, undriven_4);
  or or_1 (or_1_out, and_1_out, and_2_out, and_3_out, and_4_out);

  // Notes on the sheet:
  //   A
  //   B
  //   C
  //   D
  //   Control1
  //   Control0
  //   Y
endmodule
