// Logisim project muxadders.circ as structural Verilog: 1 circuit, main circuit main
module main (
);

  wire adder_1_cout, adder_2_cout, multiplexer_1_out, multiplexer_2_out, multiplexer_3_out, undriven_5,
       undriven_7;
  wire [1:0] undriven_6;
  wire [7:0] adder_1_out, adder_2_out, undriven, undriven_2, undriven_3, undriven_4;

  Adder adder_1 (.a(undriven), .b(undriven_2), .out(adder_1_out), .cin(undriven_5), .cout(adder_1_cout));
  Adder adder_2 (.a(undriven_3), .b(undriven_4), .out(adder_2_out), .cin(adder_1_cout), .cout(adder_2_cout));
  Multiplexer #(.select(2)) multiplexer_1 (
    .in0(undriven_5), .in1(undriven_2[0]), .in2(undriven[0]), .in3(adder_1_out[0]), .out(multiplexer_1_out),
    .sel(undriven_6), .en(undriven_7));
  Multiplexer #(.select(2)) multiplexer_2 (
    .in0(1'b0), .in1(undriven_4[0]), .in2(undriven_3[0]), .in3(adder_2_out[0]), .out(multiplexer_2_out),
    .sel(undriven_6), .en(undriven_7));
  Multiplexer #(.select(2)) multiplexer_3 (
    .in0(1'b0), .in1(1'b0), .in2(1'b0), .in3(adder_2_cout), .out(multiplexer_3_out), .sel(undriven_6),
    .en(undriven_7));
  // Pins of 1 and 8 bits meet at undriven_4
  // Pins of 1 and 8 bits meet at undriven_3
  // Pins of 1 and 8 bits meet at adder_2_out
  // Pins of 1 and 8 bits meet at undriven_2
  // Pins of 1 and 8 bits meet at undriven
  // Pins of 1 and 8 bits meet at adder_1_out

  // Notes on the sheet:
  //   A0
  //   B0
  //   A1
  //   B1
  //   Cin
  //   C1
  //   C0
  //   O0
  //   O1
  //   O2
endmodule
